// Logisim project 02 .Booths_multiplication.circ as structural Verilog: 12 circuits, main circuit Booth's multiplier
module Booth_s_multiplier (
  input  [11:0] M_input,
  input  [11:0] Q_input,
  input  Reset,
  output [11:0] Q,
  output [11:0] out_5,
  output out_6
);

  wire A_out, clock_1_out, controller_1_c0, controller_1_c1, controller_1_cl__a__q_1, controller_1_dec_cnt,
       controller_1_load__m__q__cnt, controller_1_load_a, controller_1_shr, or_1_out, Q__1_q0, Q_out;
  wire [4:0] counter_1_q;
  wire [11:0] M_q11, n4bit_alu_1_result;

  Clock clock_1 (.out(clock_1_out));
  Controller controller_1 (
    .Clk(clock_1_out), .Q0(Q[0]), .Q_1(Q__1_q0), .Count(counter_1_q), .C0(controller_1_c0),
    .C1(controller_1_c1), .Shr(controller_1_shr), .Dec_Cnt(controller_1_dec_cnt),
    .Cl__A__Q_1(controller_1_cl__a__q_1), .Load_A(controller_1_load_a),
    .LOad__M__Q__Cnt(controller_1_load__m__q__cnt), .Reset(Reset));
  or or_1 (or_1_out, controller_1_load__m__q__cnt, controller_1_dec_cnt);
  Counter #(.width(5), .max('h1f)) counter_1 (
    .load(or_1_out), .D(5'b01100), .count(controller_1_dec_cnt), .Q(counter_1_q), .clk(clock_1_out));  // open: carry, clr
  Shift_Register #(.length(12)) A (
    .shift(controller_1_shr), .in(out_5[11]), .clk(clock_1_out), .out(A_out), .load(controller_1_load_a),
    .clr(controller_1_cl__a__q_1), .d0(n4bit_alu_1_result[11]), .q0(out_5[11]), .d1(n4bit_alu_1_result[10]),
    .q1(out_5[10]), .d2(n4bit_alu_1_result[9]), .q2(out_5[9]), .d3(n4bit_alu_1_result[8]), .q3(out_5[8]),
    .d4(n4bit_alu_1_result[7]), .q4(out_5[7]), .d5(n4bit_alu_1_result[6]), .q5(out_5[6]),
    .d6(n4bit_alu_1_result[5]), .q6(out_5[5]), .d7(n4bit_alu_1_result[4]), .q7(out_5[4]),
    .d8(n4bit_alu_1_result[3]), .q8(out_5[3]), .d9(n4bit_alu_1_result[2]), .q9(out_5[2]),
    .d10(n4bit_alu_1_result[1]), .q10(out_5[1]), .d11(n4bit_alu_1_result[0]), .q11(out_5[0]));
  Comparator #(.width(5)) comparator_1 (.a(counter_1_q), .b({5{1'b0}}), .eq(out_6));  // open: gt, lt
  Shift_Register #(.length(12)) M (
    .shift(1'b0), .clk(clock_1_out), .load(controller_1_load__m__q__cnt), .d0(M_input[11]), .q0(M_q11[11]),
    .d1(M_input[10]), .q1(M_q11[10]), .d2(M_input[9]), .q2(M_q11[9]), .d3(M_input[8]), .q3(M_q11[8]),
    .d4(M_input[7]), .q4(M_q11[7]), .d5(M_input[6]), .q5(M_q11[6]), .d6(M_input[5]), .q6(M_q11[5]),
    .d7(M_input[4]), .q7(M_q11[4]), .d8(M_input[3]), .q8(M_q11[3]), .d9(M_input[2]), .q9(M_q11[2]),
    .d10(M_input[1]), .q10(M_q11[1]), .d11(M_input[0]), .q11(M_q11[0]));  // open: in, out, clr
  _4bit_ALU u_4bit_alu_1 (
    .A(out_5), .B(M_q11), .Result(n4bit_alu_1_result), .Control0(controller_1_c0), .Control1(controller_1_c1));  // open: Zero, Negative, Overflow, Carry
  Shift_Register #(.length(12)) u_Q (
    .shift(controller_1_shr), .in(A_out), .clk(clock_1_out), .out(Q_out),
    .load(controller_1_load__m__q__cnt), .d0(Q_input[11]), .q0(Q[11]), .d1(Q_input[10]), .q1(Q[10]),
    .d2(Q_input[9]), .q2(Q[9]), .d3(Q_input[8]), .q3(Q[8]), .d4(Q_input[7]), .q4(Q[7]), .d5(Q_input[6]),
    .q5(Q[6]), .d6(Q_input[5]), .q6(Q[5]), .d7(Q_input[4]), .q7(Q[4]), .d8(Q_input[3]), .q8(Q[3]),
    .d9(Q_input[2]), .q9(Q[2]), .d10(Q_input[1]), .q10(Q[1]), .d11(Q_input[0]), .q11(Q[0]));  // open: clr
  Shift_Register #(.length(1)) Q__1 (
    .shift(controller_1_shr), .in(Q_out), .clk(clock_1_out), .clr(controller_1_cl__a__q_1), .q0(Q__1_q0));  // open: out, load, d0
endmodule

// 4-bit AND
module _4_bit_and (
  input  [11:0] A,
  input  [11:0] B,
  output [11:0] Result
);

  assign Result = A & B;  // AND_Gate and_1, 12 bits wide
endmodule

// 4-bit OR
module _4_bit_OR (
  input  [11:0] A,
  input  [11:0] B,
  output [11:0] Result
);

  assign Result = A | B;  // OR_Gate or_1, 12 bits wide
endmodule

module Full_adder (
  input  Carry_in,
  input  A,
  input  B,
  output Result,
  output Carry_out
);

  wire and_1_out, and_2_out, xor_1_out;

  and and_1 (and_1_out, B, A);
  xor xor_1 (xor_1_out, A, B);
  or or_1 (Carry_out, and_1_out, and_2_out);
  and and_2 (and_2_out, xor_1_out, Carry_in);
  xor xor_2 (Result, Carry_in, xor_1_out);
endmodule

module _4_bit_full_adder (
  input  Carry_in,
  input  [11:0] A,
  input  [11:0] B,
  output [11:0] Result,
  output Carry
);

  wire full_adder_1_carry_out, full_adder_2_carry_out, full_adder_3_carry_out, full_adder_4_carry_out,
       full_adder_5_carry_out, full_adder_6_carry_out, full_adder_7_carry_out, full_adder_8_carry_out,
       full_adder_9_carry_out, full_adder_10_carry_out, full_adder_11_carry_out;

  Full_adder full_adder_1 (
    .Carry_in(Carry_in), .A(A[0]), .B(B[0]), .Result(Result[0]), .Carry_out(full_adder_1_carry_out));
  Full_adder full_adder_2 (
    .Carry_in(full_adder_1_carry_out), .A(A[1]), .B(B[1]), .Result(Result[1]),
    .Carry_out(full_adder_2_carry_out));
  Full_adder full_adder_3 (
    .Carry_in(full_adder_2_carry_out), .A(A[2]), .B(B[2]), .Result(Result[2]),
    .Carry_out(full_adder_3_carry_out));
  Full_adder full_adder_4 (
    .Carry_in(full_adder_3_carry_out), .A(A[3]), .B(B[3]), .Result(Result[3]),
    .Carry_out(full_adder_4_carry_out));
  Full_adder full_adder_5 (
    .Carry_in(full_adder_4_carry_out), .A(A[4]), .B(B[4]), .Result(Result[4]),
    .Carry_out(full_adder_5_carry_out));
  Full_adder full_adder_6 (
    .Carry_in(full_adder_5_carry_out), .A(A[5]), .B(B[5]), .Result(Result[5]),
    .Carry_out(full_adder_6_carry_out));
  Full_adder full_adder_7 (
    .Carry_in(full_adder_6_carry_out), .A(A[6]), .B(B[6]), .Result(Result[6]),
    .Carry_out(full_adder_7_carry_out));
  Full_adder full_adder_8 (
    .Carry_in(full_adder_7_carry_out), .A(A[7]), .B(B[7]), .Result(Result[7]),
    .Carry_out(full_adder_8_carry_out));
  Full_adder full_adder_9 (
    .Carry_in(full_adder_8_carry_out), .A(A[8]), .B(B[8]), .Result(Result[8]),
    .Carry_out(full_adder_9_carry_out));
  Full_adder full_adder_10 (
    .Carry_in(full_adder_9_carry_out), .A(A[9]), .B(B[9]), .Result(Result[9]),
    .Carry_out(full_adder_10_carry_out));
  Full_adder full_adder_11 (
    .Carry_in(full_adder_10_carry_out), .A(A[10]), .B(B[10]), .Result(Result[10]),
    .Carry_out(full_adder_11_carry_out));
  Full_adder full_adder_12 (
    .Carry_in(full_adder_11_carry_out), .A(A[11]), .B(B[11]), .Result(Result[11]), .Carry_out(Carry));
endmodule

module _4_bit_xor (
  input  Control,
  input  [11:0] B,
  output [11:0] Result
);

  wire [11:0] bit_extender_1_out;

  assign bit_extender_1_out = {{11{Control}}, Control};  // Bit_Extender bit_extender_1
  assign Result = bit_extender_1_out ^ B;  // XOR_Gate xor_1, 12 bits wide
endmodule

// 32-bit \nADD/SUB
module Add_sub (
  input  Sub,
  input  [11:0] A,
  input  [11:0] B,
  output [11:0] Result,
  output Carry,
  output Overflow
);

  wire and_1_out, and_2_out, not_1_out, not_2_out, not_3_out, sign_bit_out_1_ms_bit, sign_bit_out_2_ms_bit,
       sign_bit_out_3_ms_bit;
  wire [11:0] n4_bit_xor_1_result;

  sign_bit_out sign_bit_out_1 (.Input(A), .MS_bit(sign_bit_out_1_ms_bit));
  not not_1 (not_1_out, sign_bit_out_1_ms_bit);
  _4_bit_xor u_4_bit_xor_1 (.B(B), .Result(n4_bit_xor_1_result), .Control(Sub));
  sign_bit_out sign_bit_out_2 (.Input(n4_bit_xor_1_result), .MS_bit(sign_bit_out_2_ms_bit));
  not not_2 (not_2_out, sign_bit_out_2_ms_bit);
  _4_bit_full_adder u_4_bit_full_adder_1 (
    .A(A), .B(n4_bit_xor_1_result), .Result(Result), .Carry_in(Sub), .Carry(Carry));
  sign_bit_out sign_bit_out_3 (.Input(Result), .MS_bit(sign_bit_out_3_ms_bit));
  not not_3 (not_3_out, sign_bit_out_3_ms_bit);
  and and_1 (and_1_out, not_3_out, sign_bit_out_2_ms_bit, sign_bit_out_1_ms_bit);
  and and_2 (and_2_out, sign_bit_out_3_ms_bit, not_2_out, not_1_out);
  or or_1 (Overflow, and_1_out, and_2_out);

  // Notes on the sheet:
  //   A31
  //   B31
  //   Result 31
endmodule

// 31th
module sign_bit_out (
  input  [11:0] Input,
  output MS_bit
);


  assign MS_bit = Input[11];
endmodule

// Reduce-OR
module _4_bit_reduce_or (
  input  [11:0] Input,
  output Output
);

  or or_1 (Output, Input[2], Input[3], Input[4], Input[0], Input[1], Input[10], Input[11], Input[5], Input[6], Input[7], Input[8], Input[9]);
endmodule

// 4 bit ALU
module _4bit_ALU (
  input  Control0,
  input  Control1,
  input  [11:0] A,
  input  [11:0] B,
  output [11:0] Result,
  output Zero,
  output Negative,
  output Overflow,
  output Carry
);

  wire n4_bit_reduce_or_1_output;
  wire [11:0] add_sub_1_result, multiplexer_1_out, n4_bit_and_1_result, n4_bit_or_1_result;

  _4_bit_and u_4_bit_and_1 (.A(A), .B(B), .Result(n4_bit_and_1_result));
  _4_bit_OR u_4_bit_or_1 (.A(A), .B(B), .Result(n4_bit_or_1_result));
  Add_sub add_sub_1 (.Sub(Control0), .A(A), .B(B), .Result(add_sub_1_result), .Carry(Carry), .Overflow(Overflow));
  Multiplexer #(.width(12), .enable("false")) multiplexer_1 (
    .in0(n4_bit_and_1_result), .in1(n4_bit_or_1_result), .out(multiplexer_1_out), .sel(Control0));
  Multiplexer #(.width(12), .enable("false")) multiplexer_2 (
    .in0(multiplexer_1_out), .in1(add_sub_1_result), .out(Result), .sel(Control1));
  sign_bit_out sign_bit_out_1 (.Input(Result), .MS_bit(Negative));
  _4_bit_reduce_or u_4_bit_reduce_or_1 (.Input(Result), .Output(n4_bit_reduce_or_1_output));
  not not_1 (Zero, n4_bit_reduce_or_1_output);
endmodule

// Control \nUnit
module Controller (
  input  Clk,
  input  Reset,
  input  Q0,
  input  Q_1,
  input  [4:0] Count,
  output Cl__A__Q_1,
  output LOad__M__Q__Cnt,
  output Load_A,
  output C0,
  output C1,
  output Shr,
  output Dec_Cnt
);

  wire and_3_out, multiplexer_1_out, not_1_out, not_2_out, not_3_out, not_4_out, not_5_out, not_6_out,
       not_7_out, or_2_out, Q0_prime_Q_1_out, Q0Q_1_prime_out;
  wire [1:0] rom_1_data_2;
  wire [2:0] and_1_out, and_2_out, bit_extender_1_out, bit_extender_2_out, bit_extender_3_out, CAR_q,
       or_1_out, rom_1_data;

  assign bit_extender_1_out = {{2{Q0_prime_Q_1_out}}, Q0_prime_Q_1_out};  // Bit_Extender bit_extender_1
  and Q0_prime_Q_1 (Q0_prime_Q_1_out, not_2_out, Q_1);
  not not_1 (not_1_out, Q0_prime_Q_1_out);
  assign bit_extender_2_out = {{2{not_1_out}}, not_1_out};  // Bit_Extender bit_extender_2
  assign and_1_out = 3'b100 & bit_extender_3_out & bit_extender_1_out;  // AND_Gate and_1, 3 bits wide
  assign or_1_out = and_1_out | rom_1_data | and_2_out;  // OR_Gate or_1, 3 bits wide
  not not_2 (not_2_out, Q0);
  assign and_2_out = bit_extender_2_out & bit_extender_3_out & 3'b101;  // AND_Gate and_2, 3 bits wide
  assign bit_extender_3_out = {{2{and_3_out}}, and_3_out};  // Bit_Extender bit_extender_3
  and and_3 (and_3_out, not_3_out, CAR_q[1], not_4_out);
  not not_3 (not_3_out, CAR_q[2]);
  not not_4 (not_4_out, CAR_q[0]);
  Counter #(.width(3), .max('h7)) CAR (
    .load(not_5_out), .D(or_1_out), .count(multiplexer_1_out), .Q(CAR_q), .clk(Clk), .clr(Reset));  // open: carry
  not not_5 (not_5_out, multiplexer_1_out);
  Multiplexer #(.select(2), .enable("false")) multiplexer_1 (
    .in0(1'b0), .in1(1'b1), .in2(Q0Q_1_prime_out), .in3(not_7_out), .out(multiplexer_1_out),
    .sel(rom_1_data_2));
  ROM #(.addrWidth(3), .dataWidth(12)) rom_1 (
    .addr(CAR_q), .data({Cl__A__Q_1, LOad__M__Q__Cnt, Load_A, C0, C1, Shr, Dec_Cnt, rom_1_data, rom_1_data_2}));  // open: sel
  and Q0Q_1_prime (Q0Q_1_prime_out, not_6_out, Q0);
  not not_6 (not_6_out, Q_1);
  not not_7 (not_7_out, or_2_out);
  or or_2 (or_2_out, Count[0], Count[1], Count[2], Count[3], Count[4]);

  // Notes on the sheet:
  //   To choose only
  //   state 2 (010)
  //   Control Word Format: Clear (A, Q-1), Load (M, Q, Cnt), Load A, C0, C1, Shr, Dec Cnt, Address bits (3 bit), Selection bits (2 bit)
  //   contents of rom_1 (hex, n*v repeats v):
  //   1 c01 2 394 281 61 b 1c
endmodule

module _1 (
);

  Counter counter_1 ();  // open: load, D, count, Q, carry, clk, clr
endmodule
