// Logisim project 03 . 12-bit-ALU.circ as structural Verilog: 10 circuits, main circuit main
module main (
  input  [3:0] in_1,
  input  [11:0] A,
  input  [11:0] B,
  output [11:0] Result,
  output Zero,
  output Negative,
  output Overflow,
  output Carry
);

  wire n8_bit_reduce_or_1_output;
  wire [11:0] add_sub_1_result, add_sub_2_result, n8_bit_and_1_result, n8_bit_or_1_result, shifter_1_out,
       shifter_2_out, xor_1_out_3;

  Shifter #(.width(12)) shifter_1 (.in(A), .\dist (4'b0001), .out(shifter_1_out));
  Shifter #(.width(12), .shift("ar")) shifter_2 (.in(A), .\dist (4'b0001), .out(shifter_2_out));
  _8_bit_and u_8_bit_and_1 (.A(A), .B(B), .Result(n8_bit_and_1_result));
  _8_bit_OR u_8_bit_or_1 (.A(A), .B(B), .Result(n8_bit_or_1_result));
  Add_sub add_sub_1 (.Sub(in_1[1]), .A(A), .B(B), .Result(add_sub_1_result), .Carry(Carry), .Overflow(Overflow));
  XOR xor_1 (.in_1(A), .in_2(B), .out_3(xor_1_out_3));
  Add_sub add_sub_2 (.Sub(in_1[0]), .A(A), .B(12'h1), .Result(add_sub_2_result));  // open: Carry, Overflow
  Multiplexer #(.select(4), .width(12), .enable("false")) multiplexer_1 (
    .in0(n8_bit_and_1_result), .in1(add_sub_1_result), .in2(n8_bit_or_1_result), .in3(add_sub_1_result),
    .in4(xor_1_out_3), .in5(shifter_1_out), .in6(add_sub_2_result), .in7(add_sub_2_result),
    .in8(shifter_2_out), .out(Result), .sel(in_1));  // open: in9, in10, in11, in12, in13, in14, in15
  _7th_bit_out u_7th_bit_out_1 (.Input(Result), ._7th_bit(Negative));
  _8_bit_reduce_or u_8_bit_reduce_or_1 (.Input(Result), .Output(n8_bit_reduce_or_1_output));
  not not_1 (Zero, n8_bit_reduce_or_1_output);
endmodule

// 8-bit AND
module _8_bit_and (
  input  [11:0] A,
  input  [11:0] B,
  output [11:0] Result
);

  assign Result = A & B;  // AND_Gate and_1, 12 bits wide
endmodule

// 8-bit OR
module _8_bit_OR (
  input  [11:0] A,
  input  [11:0] B,
  output [11:0] Result
);

  assign Result = A | B;  // OR_Gate or_1, 12 bits wide
endmodule

module Full_adder (
  input  Carry_in,
  input  A,
  input  B,
  output Result,
  output Carry_out
);

  wire and_1_out, and_2_out, xor_1_out;

  and and_1 (and_1_out, B, A);
  xor xor_1 (xor_1_out, A, B);
  or or_1 (Carry_out, and_1_out, and_2_out);
  and and_2 (and_2_out, xor_1_out, Carry_in);
  xor xor_2 (Result, Carry_in, xor_1_out);
endmodule

module _8_bit_full_adder (
  input  Carry_in,
  input  [11:0] A,
  input  [11:0] B,
  output [11:0] Result,
  output Carry
);

  wire full_adder_1_carry_out, full_adder_2_carry_out, full_adder_3_carry_out, full_adder_4_carry_out,
       full_adder_5_carry_out, full_adder_6_carry_out, full_adder_7_carry_out, full_adder_8_carry_out,
       full_adder_9_carry_out, full_adder_10_carry_out, full_adder_11_carry_out;

  Full_adder full_adder_1 (
    .Carry_in(Carry_in), .A(A[0]), .B(B[0]), .Result(Result[0]), .Carry_out(full_adder_1_carry_out));
  Full_adder full_adder_2 (
    .Carry_in(full_adder_1_carry_out), .A(A[1]), .B(B[1]), .Result(Result[1]),
    .Carry_out(full_adder_2_carry_out));
  Full_adder full_adder_3 (
    .Carry_in(full_adder_2_carry_out), .A(A[2]), .B(B[2]), .Result(Result[2]),
    .Carry_out(full_adder_3_carry_out));
  Full_adder full_adder_4 (
    .Carry_in(full_adder_3_carry_out), .A(A[3]), .B(B[3]), .Result(Result[3]),
    .Carry_out(full_adder_4_carry_out));
  Full_adder full_adder_5 (
    .Carry_in(full_adder_4_carry_out), .A(A[4]), .B(B[4]), .Result(Result[4]),
    .Carry_out(full_adder_5_carry_out));
  Full_adder full_adder_6 (
    .Carry_in(full_adder_5_carry_out), .A(A[5]), .B(B[5]), .Result(Result[5]),
    .Carry_out(full_adder_6_carry_out));
  Full_adder full_adder_7 (
    .Carry_in(full_adder_6_carry_out), .A(A[6]), .B(B[6]), .Result(Result[6]),
    .Carry_out(full_adder_7_carry_out));
  Full_adder full_adder_8 (
    .Carry_in(full_adder_7_carry_out), .A(A[7]), .B(B[7]), .Result(Result[7]),
    .Carry_out(full_adder_8_carry_out));
  Full_adder full_adder_9 (
    .Carry_in(full_adder_8_carry_out), .A(A[8]), .B(B[8]), .Result(Result[8]),
    .Carry_out(full_adder_9_carry_out));
  Full_adder full_adder_10 (
    .Carry_in(full_adder_9_carry_out), .A(A[9]), .B(B[9]), .Result(Result[9]),
    .Carry_out(full_adder_10_carry_out));
  Full_adder full_adder_11 (
    .Carry_in(full_adder_10_carry_out), .A(A[10]), .B(B[10]), .Result(Result[10]),
    .Carry_out(full_adder_11_carry_out));
  Full_adder full_adder_12 (
    .Carry_in(full_adder_11_carry_out), .A(A[11]), .B(B[11]), .Result(Result[11]), .Carry_out(Carry));
endmodule

module _8_bit_xor (
  input  Control,
  input  [11:0] B,
  output [11:0] Result
);

  wire [11:0] bit_extender_1_out;

  assign bit_extender_1_out = {{11{Control}}, Control};  // Bit_Extender bit_extender_1
  assign Result = bit_extender_1_out ^ B;  // XOR_Gate xor_1, 12 bits wide
endmodule

// 8-bit \nADD/SUB
module Add_sub (
  input  Sub,
  input  [11:0] A,
  input  [11:0] B,
  output [11:0] Result,
  output Carry,
  output Overflow
);

  wire and_1_out, and_2_out, n7th_bit_out_1__7th_bit, n7th_bit_out_2__7th_bit, n7th_bit_out_3__7th_bit,
       not_1_out, not_2_out, not_3_out;
  wire [11:0] n8_bit_xor_1_result;

  _7th_bit_out u_7th_bit_out_1 (.Input(A), ._7th_bit(n7th_bit_out_1__7th_bit));
  not not_1 (not_1_out, n7th_bit_out_1__7th_bit);
  _8_bit_xor u_8_bit_xor_1 (.B(B), .Result(n8_bit_xor_1_result), .Control(Sub));
  _7th_bit_out u_7th_bit_out_2 (.Input(n8_bit_xor_1_result), ._7th_bit(n7th_bit_out_2__7th_bit));
  not not_2 (not_2_out, n7th_bit_out_2__7th_bit);
  _8_bit_full_adder u_8_bit_full_adder_1 (
    .A(A), .B(n8_bit_xor_1_result), .Result(Result), .Carry_in(Sub), .Carry(Carry));
  _7th_bit_out u_7th_bit_out_3 (.Input(Result), ._7th_bit(n7th_bit_out_3__7th_bit));
  not not_3 (not_3_out, n7th_bit_out_3__7th_bit);
  and and_1 (and_1_out, not_3_out, n7th_bit_out_2__7th_bit, n7th_bit_out_1__7th_bit);
  and and_2 (and_2_out, n7th_bit_out_3__7th_bit, not_2_out, not_1_out);
  or or_1 (Overflow, and_1_out, and_2_out);

  // Notes on the sheet:
  //   A31
  //   B31
  //   Result 31
endmodule

// 7th
module _7th_bit_out (
  input  [11:0] Input,
  output _7th_bit
);


  assign _7th_bit = Input[11];
endmodule

// Reduce-OR
module _8_bit_reduce_or (
  input  [11:0] Input,
  output Output
);

  or or_1 (Output, Input[8], Input[9], Input[0], Input[1], Input[2], Input[3], Input[5], Input[6], Input[7], Input[4], Input[10], Input[11]);
endmodule

// xor
module XOR (
  input  [11:0] in_1,
  input  [11:0] in_2,
  output [11:0] out_3
);

  assign out_3 = in_1 ^ in_2;  // XOR_Gate xor_1, 12 bits wide
endmodule
