// Logisim project CPU_demo.circ as structural Verilog: 3 circuits, main circuit main
module main (
);

  wire clock_1_out, cpu_1_r, cpu_1_w, Reset_out;
  wire [7:0] cpu_1_addr;
  wire [11:0] cpu_1_dataout, ram_1_data;

  Clock clock_1 (.out(clock_1_out));
  Button Reset (.out(Reset_out));
  CPU cpu_1 (
    .Clk(clock_1_out), .Reset(Reset_out), .R(cpu_1_r), .W(cpu_1_w), .Addr(cpu_1_addr), .DataIn(ram_1_data),
    .DataOut(cpu_1_dataout));
  RAM #(.dataWidth(12), .bus("separate")) ram_1 (
    .addr(cpu_1_addr), .din(cpu_1_dataout), .data(ram_1_data), .str(cpu_1_w), .clk(clock_1_out), .ld(cpu_1_r));  // open: sel, clr

  // Notes on the sheet:
  //               8 -  XOR
  //   0 - AND
  //                   A  =  DEC
  //   1 - ADD
  //             B =SHL
  //   2 - STO
  //                 C = SHR
  //   3 - OR
  //              D = MUL
  //   4 - SUB
  //   5 - BUN
  //   6 - LDA
  //   7 - HLT
  //   9 - INC
endmodule

module CPU (
  input  Clk,
  input  Reset,
  input  [11:0] DataIn,
  output R,
  output W,
  output [7:0] Addr,
  output [11:0] DataOut
);

  wire b1, controlunit_1_c1, controlunit_1_c2, d1, d2, done, LdA, LdA_from_MBR, LoadAc, LoadB, LoadMAR,
       mul_set, rst;
  wire [3:0] c0;
  wire [7:0] counter_1_q, multiplexer_1_out;
  wire [11:0] Ac, AcIn, ALUout, mul_out, multiplexer_2_out, multiplexer_4_out;

  Multiplexer #(.width(8), .enable("false")) multiplexer_1 (
    .in0(counter_1_q), .in1(DataOut[7:0]), .out(multiplexer_1_out), .sel(d2));
  Multiplexer #(.width(12), .enable("false")) multiplexer_2 (
    .in0(ALUout), .in1(DataOut), .out(multiplexer_2_out), .sel(LdA_from_MBR));
  Counter counter_1 (
    .load(controlunit_1_c2), .D(DataOut[7:0]), .count(controlunit_1_c1), .Q(counter_1_q), .clk(Clk),
    .clr(Reset));  // open: carry
  Register MAR (.D(multiplexer_1_out), .en(LoadMAR), .Q(Addr), .clk(Clk), .clr(Reset));
  Register #(.width(4)) IR (.D(DataOut[11:8]), .en(controlunit_1_c1), .clk(Clk), .clr(Reset));  // open: Q
  ControlUnit controlunit_1 (
    .IR(DataOut[11:8]), .Clk(Clk), .d1(d1), .c1(controlunit_1_c1), .R(R), .d2(d2), .b1(b1), .W(W),
    .LdAfrB(LdA_from_MBR), .LoadAc(LdA), .Reset(Reset), .c2(controlunit_1_c2), .Operation(c0),
    .mul_set(mul_set), .rst(rst), .done(done));  // open: b2, b3
  Multiplexer #(.width(12), .enable("false")) multiplexer_3 (
    .in0(multiplexer_2_out), .in1(mul_out), .out(AcIn), .sel(mul_set));
  Multiplexer #(.width(12), .enable("false")) multiplexer_4 (.in0(DataIn), .in1(Ac), .out(multiplexer_4_out), .sel(b1));
  or or_1 (LoadMAR, d1, d2);
  Register #(.width(12)) MBR (.D(multiplexer_4_out), .en(LoadB), .Q(DataOut), .clk(Clk), .clr(Reset));
  Register #(.width(12)) u_Ac (.D(AcIn), .en(LoadAc), .Q(Ac), .clk(Clk), .clr(Reset));
  // _8_bit_ALU_main main_1: pin names not known; wires that end beside it: c0, Ac, DataOut, ALUout
  or or_2 (LoadB, R, b1);
  or or_3 (LoadAc, LdA_from_MBR, LdA);
  // Booth_s_multiplier booth_s_multiplier_1: pin names not known; wires that end beside it: Ac, rst, DataOut, done, mul_out

  // Other names for the same wires on the sheet: clr = Reset; MBRout[11:0] = DataOut
endmodule

// CU
module ControlUnit (
  input  [3:0] IR,
  input  Clk,
  input  Reset,
  input  done,
  output d1,
  output c1,
  output R,
  output c2,
  output d2,
  output [3:0] Operation,
  output b1,
  output W,
  output b2,
  output b3,
  output LdAfrB,
  output LoadAc,
  output mul_set,
  output rst
);

  wire and_1_out, and_2_out, decoder_1_out6, decoder_1_out7, decoder_1_out8, decoder_1_out9, decoder_1_out15,
       decoder_1_out16, decoder_1_out17, decoder_1_out18, decoder_1_out19, decoder_1_out20, not_1_out,
       or_1_out;
  wire [5:0] counter_1_q;
  wire [7:0] rom_1_data;

  Counter #(.width(6), .max('h3f)) counter_1 (
    .load(rom_1_data[2]), .D({IR, 2'b11}), .count(rom_1_data[0]), .Q(counter_1_q), .clk(and_1_out),
    .clr(or_1_out));  // open: carry
  or or_1 (or_1_out, rom_1_data[1], Reset);
  and and_1 (and_1_out, Clk, and_2_out);
  and and_2 (and_2_out, done, not_1_out);
  ROM #(.addrWidth(6)) rom_1 (.addr(counter_1_q), .data(rom_1_data));  // open: sel
  not not_1 (not_1_out, decoder_1_out15);
  Decoder #(.select(5), .enable("false")) decoder_1 (
    .out1(d1), .out2(c1), .out3(R), .out4(c2), .out5(d2), .out6(decoder_1_out6), .out7(decoder_1_out7),
    .out8(decoder_1_out8), .out9(decoder_1_out9), .out10(b1), .out11(W), .out12(b2), .out13(b3),
    .out14(LdAfrB), .out15(decoder_1_out15), .out16(decoder_1_out16), .out17(decoder_1_out17),
    .out18(decoder_1_out18), .out19(decoder_1_out19), .out20(decoder_1_out20), .out21(mul_set), .out22(rst),
    .sel(rom_1_data[7:3]));  // open: out0, out23, out24, out25, out26, out27, out28, out29, out30, out31
  Priority_Encoder #(.select(4)) priority_encoder_1 (
    .in0(decoder_1_out6), .in1(decoder_1_out7), .in2(decoder_1_out8), .in3(decoder_1_out9),
    .in4(decoder_1_out16), .in5(decoder_1_out19), .in6(decoder_1_out17), .in7(decoder_1_out18),
    .in8(decoder_1_out20), .out(Operation));  // open: in9, in10, in11, in12, in13, in14, in15, gs, en_out, en_in
  or or_2 (LoadAc, decoder_1_out8, decoder_1_out20, decoder_1_out18, decoder_1_out6, decoder_1_out7, decoder_1_out9, decoder_1_out16, decoder_1_out17, decoder_1_out19, mul_set);

  // Notes on the sheet:
  //   contents of rom_1 (hex, n*v repeats v):
  //   9 19 14 29 19 31 2 29 19 39 2 29 51 59 2 29 19 41 2 29 19 49 2 21 2 2 2 29 19 71 2 78 2 2 2 29 19 81
  //   2 89 2 2 2 91 2 2 2 99 2 2 2 a1 2 2 2 29 19 b1 1 1 1 a9 2 2
endmodule
